# Fritzing sketch laba (saved by Fritzing 0.9.3b)
breadboards: 1

parts:
  Часть1 = Arduino Uno (Rev3)
  AM1 = AM2302 Humidity and Temperature Sensor
  Часть2 = Adafruit DS3231 [part_number="Adafruit #3013"]  # not connected
  hc-sr1 = hc-sr04  # not connected
  microSD_Transflash1 = SparkFun - microSD Transflash  # not connected

nets:
  N1: Часть1.D2, AM1.DATA
  5V: Часть1.5V, AM1.VDD
  GND: Часть1.GND, AM1.GND

custom parts:
  Adafruit DS3231: The datasheet for the DS3231 explains that this part is an "Extremely Accurate I²C-Integrated RTC/TCXO/Crystal". And, hey, it does exactly what it says on the tin! This Real Time Clock (RTC) is the most precise you can get in a small, low power package. Most RTCs use an external 32kHz timing crystal that is used to keep time with low current draw. And that's all well and good, but those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
